# Fritzing sketch iMissYou (saved by Fritzing 0.9.2b)
breadboards: 1

parts:
  Part1 = Arduino Yun
  R1 = Resistor [tolerance=±5% resistance=220 package=THT]
  LED1 = LED - 5mm [color="Green (555nm)" package="5 mm [THT]"]
  LED2 = LED - 5mm [color="Red (633nm)" package="5 mm [THT]"]
  R2 = Resistor [tolerance=±5% resistance=220 package=THT]
  R3 = Resistor [tolerance=±5% resistance=220 package=THT]
  U1 = CAPSENSE_PAD [package=capsense_pad]  # not connected

nets:
  N1: Part1.D8, LED1.anode
  N2: Part1.D9_PWM, LED2.anode
  N3: Part1.GND, LED1.cathode, LED2.cathode, R2.Pin_0, R2.Pin_1, R3.Pin_0, R3.Pin_1
  N4: Part1.D4, R1.Pin_0, R1.Pin_1

notes:
  Connect these wires to your conductive layer
